// Logisim project 8-bit-alu.circ as structural Verilog: 7 circuits, main circuit ALU
module ALU (
  input  R,
  input  L,
  input  C,
  input  F2,
  input  F1,
  input  F0,
  input  Cin,
  input  M,
  input  Q7,
  input  in_10,
  input  in_11,
  input  in_12,
  input  in_13,
  input  in_14,
  input  in_15,
  input  Q0,
  input  P7,
  input  in_18,
  input  in_19,
  input  in_20,
  input  in_21,
  input  in_22,
  input  in_23,
  input  P0,
  input  Odd,
  output P_Q,
  output P_Q_2,
  output H,
  output V,
  output P,
  output Z,
  output S,
  output C_2,
  output X7,
  output out_35,
  output out_36,
  output out_37,
  output out_38,
  output out_39,
  output out_40,
  output X0
);

  wire and_2_out, n1_bit_1_cout, n1_bit_2_cout, n1_bit_3_cout, n1_bit_4_cout, n1_bit_5_cout, n1_bit_6_cout,
       n1_bit_7_cout, not_1_out, or_1_out;
  wire [3:0] n1_bit_1_s, n1_bit_5_s, q_xor_m_1_q0_prime, q_xor_m_1_q4_prime;

  Parity parity_1 (.Odd(Odd), .C(n1_bit_4_cout), .Parity(P), .X4__7(n1_bit_1_s), .X0__3(n1_bit_5_s));
  and and_1 (S, M, n1_bit_1_s[3]);
  not not_1 (not_1_out, M);
  and and_2 (and_2_out, not_1_out, n1_bit_4_cout);
  Zero zero_1 (.X0__3(n1_bit_5_s), .Zero(Z), .X4__7(n1_bit_1_s), .C(and_2_out));
  _1_bit u_1_bit_1 (
    .F2(F2), .F1(F1), .F0(F0), .Cin(H), .Q(q_xor_m_1_q4_prime[0]), .P(in_20), .Cout(n1_bit_1_cout),
    .S(n1_bit_1_s[0]));
  _1_bit u_1_bit_2 (
    .F2(F2), .F1(F1), .F0(F0), .Cin(n1_bit_1_cout), .Q(q_xor_m_1_q4_prime[1]), .P(in_19),
    .Cout(n1_bit_2_cout), .S(n1_bit_1_s[1]));
  _1_bit u_1_bit_3 (
    .F2(F2), .F1(F1), .F0(F0), .Cin(n1_bit_2_cout), .Q(q_xor_m_1_q4_prime[2]), .P(in_18),
    .Cout(n1_bit_3_cout), .S(n1_bit_1_s[2]));
  _1_bit u_1_bit_4 (
    .F2(F2), .F1(F1), .F0(F0), .Cin(n1_bit_3_cout), .Q(q_xor_m_1_q4_prime[3]), .P(P7), .Cout(n1_bit_4_cout),
    .S(n1_bit_1_s[3]));
  xor xor_1 (V, n1_bit_4_cout, n1_bit_3_cout);
  Shift_register shift_register_1 (
    .R(R), .L(L), .C(C), .Carry(n1_bit_4_cout), .X7(n1_bit_1_s[3]), .X6(n1_bit_1_s[2]), .X5(n1_bit_1_s[1]),
    .X4(n1_bit_1_s[0]), .X3(n1_bit_5_s[3]), .X2(n1_bit_5_s[2]), .X1(n1_bit_5_s[1]), .X0(n1_bit_5_s[0]),
    .Carry_prime(C_2), .X7_prime(X7), .X6_prime(out_35), .X5_prime(out_36), .X4_prime(out_37),
    .X3_prime(out_38), .X2_prime(out_39), .X1_prime(out_40), .X0_prime(X0));
  or or_1 (or_1_out, Cin, M);
  _1_bit u_1_bit_5 (
    .F2(F2), .F1(F1), .F0(F0), .Cin(or_1_out), .Q(q_xor_m_1_q0_prime[0]), .P(P0), .Cout(n1_bit_5_cout),
    .S(n1_bit_5_s[0]));
  _1_bit u_1_bit_6 (
    .F2(F2), .F1(F1), .F0(F0), .Cin(n1_bit_5_cout), .Q(q_xor_m_1_q0_prime[1]), .P(in_23),
    .Cout(n1_bit_6_cout), .S(n1_bit_5_s[1]));
  _1_bit u_1_bit_7 (
    .F2(F2), .F1(F1), .F0(F0), .Cin(n1_bit_6_cout), .Q(q_xor_m_1_q0_prime[2]), .P(in_22),
    .Cout(n1_bit_7_cout), .S(n1_bit_5_s[2]));
  _1_bit u_1_bit_8 (
    .F2(F2), .F1(F1), .F0(F0), .Cin(n1_bit_7_cout), .Q(q_xor_m_1_q0_prime[3]), .P(in_21), .Cout(H),
    .S(n1_bit_5_s[3]));
  Q_XOR_M q_xor_m_1 (
    .M(M), .Q7(Q7), .Q6(in_10), .Q5(in_11), .Q4(in_12), .Q3(in_13), .Q2(in_14), .Q1(in_15), .Q0(Q0),
    .Q7_prime(q_xor_m_1_q4_prime[3]), .Q6_prime(q_xor_m_1_q4_prime[2]), .Q5_prime(q_xor_m_1_q4_prime[1]),
    .Q4_prime(q_xor_m_1_q4_prime[0]), .Q3_prime(q_xor_m_1_q0_prime[3]), .Q2_prime(q_xor_m_1_q0_prime[2]),
    .Q1_prime(q_xor_m_1_q0_prime[1]), .Q0_prime(q_xor_m_1_q0_prime[0]));
  CMP cmp_1 (
    .Q0(Q0), .P0(P0), .Q1(in_15), .P1(in_23), .Q2(in_14), .P2(in_22), .Q3(in_13), .P3(in_21), .Q4(in_12),
    .P4(in_20), .Q5(in_11), .P5(in_19), .Q6(in_10), .P6(in_18), .Q7(Q7), .P7(P7), .P_Q(P_Q_2), .P_Q_2(P_Q));

  // Notes on the sheet:
  //   8 BIT ALU :: FUNCTIONS
  //   000 :: ADD / M=1 SUB / Cin=1 INC
  //   001 :: AND
  //   010 :: NOT A
  //   011 :: NAND
  //   100 :: OR
  //   101 :: XOR
  //   110 :: NOR
  //   111 :: XNOR
  //   100 :: LSR
  //   010 :: LSL
  //   101 :: CSR
  //   011 :: CSL
endmodule

module CMP (
  input  Q0,
  input  P0,
  input  Q1,
  input  P1,
  input  Q2,
  input  P2,
  input  Q3,
  input  P3,
  input  Q4,
  input  P4,
  input  Q5,
  input  P5,
  input  Q6,
  input  P6,
  input  Q7,
  input  P7,
  output P_Q,
  output P_Q_2
);

  wire and_1_out, and_2_out, and_3_out, and_4_out, and_5_out, and_6_out, and_7_out, and_8_out, xor_1_out,
       xor_2_out, xor_3_out, xor_4_out, xor_5_out, xor_6_out, xor_7_out, xor_8_out;

  xor xor_1 (xor_1_out, Q0, ~P0);  // XOR_Gate
  xor xor_2 (xor_2_out, Q1, ~P1);  // XOR_Gate
  xor xor_3 (xor_3_out, Q2, ~P2);  // XOR_Gate
  xor xor_4 (xor_4_out, Q3, ~P3);  // XOR_Gate
  xor xor_5 (xor_5_out, Q4, ~P4);  // XOR_Gate
  xor xor_6 (xor_6_out, Q5, ~P5);  // XOR_Gate
  xor xor_7 (xor_7_out, Q6, ~P6);  // XOR_Gate
  xor xor_8 (xor_8_out, Q7, ~P7);  // XOR_Gate
  and and_1 (and_1_out, xor_2_out, xor_3_out, xor_4_out, xor_5_out, xor_6_out, xor_7_out, xor_8_out, ~Q0, P0);  // AND_Gate
  and and_2 (and_2_out, xor_3_out, xor_4_out, xor_5_out, xor_6_out, xor_7_out, xor_8_out, ~Q1, P1);  // AND_Gate
  and and_3 (and_3_out, xor_4_out, xor_5_out, xor_6_out, xor_7_out, xor_8_out, ~Q2, P2);  // AND_Gate
  and and_4 (and_4_out, xor_5_out, xor_6_out, xor_7_out, xor_8_out, ~Q3, P3);  // AND_Gate
  and and_5 (and_5_out, xor_6_out, xor_7_out, xor_8_out, ~Q4, P4);  // AND_Gate
  and and_6 (and_6_out, xor_7_out, xor_8_out, ~Q5, P5);  // AND_Gate
  and and_7 (and_7_out, xor_8_out, ~Q6, P6);  // AND_Gate
  and and_8 (and_8_out, ~Q7, P7);  // AND_Gate
  and and_9 (P_Q, xor_1_out, xor_2_out, xor_3_out, xor_4_out, xor_5_out, xor_6_out, xor_7_out, xor_8_out);
  or or_1 (P_Q_2, and_1_out, and_2_out, and_3_out, and_4_out, and_5_out, and_6_out, and_7_out, and_8_out);
endmodule

module Q_XOR_M (
  input  Q7,
  input  Q6,
  input  Q5,
  input  Q4,
  input  Q3,
  input  Q2,
  input  Q1,
  input  Q0,
  input  M,
  output Q7_prime,
  output Q6_prime,
  output Q5_prime,
  output Q4_prime,
  output Q3_prime,
  output Q2_prime,
  output Q1_prime,
  output Q0_prime
);

  xor xor_1 (Q6_prime, Q6, M);
  xor xor_2 (Q7_prime, Q7, M);
  xor xor_3 (Q4_prime, Q4, M);
  xor xor_4 (Q5_prime, Q5, M);
  xor xor_5 (Q2_prime, Q2, M);
  xor xor_6 (Q3_prime, Q3, M);
  xor xor_7 (Q1_prime, Q1, M);
  xor xor_8 (Q0_prime, Q0, M);
endmodule

module _1_bit (
  input  F2,
  input  F1,
  input  F0,
  input  Cin,
  input  Q,
  input  P,
  output Cout,
  output S
);

  wire and_1_out, and_2_out, and_3_out, and_4_out, and_5_out, and_6_out, and_7_out, and_8_out, and_9_out,
       and_10_out, and_11_out, and_12_out, and_13_out, and_14_out, and_15_out, not_1_out, not_2_out,
       not_3_out, not_4_out, not_5_out, not_6_out;

  not not_1 (not_1_out, F2);
  not not_2 (not_2_out, F1);
  not not_3 (not_3_out, F0);
  not not_4 (not_4_out, Cin);
  not not_5 (not_5_out, Q);
  not not_6 (not_6_out, P);
  and and_1 (and_1_out, not_1_out, not_2_out, not_3_out, P, Q);
  and and_2 (and_2_out, not_1_out, not_2_out, not_3_out, P, Cin);
  and and_3 (and_3_out, not_1_out, not_2_out, not_3_out, Q, Cin);
  and and_4 (and_4_out, not_2_out, not_3_out, not_4_out, not_5_out, P);
  and and_5 (and_5_out, not_2_out, not_3_out, not_4_out, not_6_out, Q);
  and and_6 (and_6_out, not_1_out, not_3_out, not_5_out, not_6_out, Cin);
  and and_7 (and_7_out, not_2_out, not_3_out, P, Q, Cin);
  and and_8 (and_8_out, not_1_out, not_2_out, P, Q, F0);
  and and_9 (and_9_out, not_1_out, not_6_out, F1);
  and and_10 (and_10_out, not_5_out, not_6_out, F1);
  and and_11 (and_11_out, not_1_out, not_5_out, F0, F1);
  and and_12 (and_12_out, not_2_out, not_5_out, P, F2);
  and and_13 (and_13_out, not_2_out, not_3_out, Q, F2);
  and and_14 (and_14_out, not_2_out, not_6_out, Q, F2);
  and and_15 (and_15_out, P, Q, F0, F1, F2);
  or or_1 (Cout, and_1_out, and_2_out, and_3_out);
  or or_2 (S, and_4_out, and_5_out, and_6_out, and_7_out, and_8_out, and_9_out, and_10_out, and_11_out, and_12_out, and_13_out, and_14_out, and_15_out);
endmodule

module Zero (
  input  C,
  input  [3:0] X4__7,
  input  [3:0] X0__3,
  output Zero
);

  nor nor_1 (Zero, C, X4__7[3], X4__7[2], X4__7[1], X4__7[0], X0__3[3], X0__3[2], X0__3[1], X0__3[0]);
endmodule

module Shift_register (
  input  Carry,
  input  X7,
  input  X6,
  input  X5,
  input  X4,
  input  X3,
  input  X2,
  input  X1,
  input  X0,
  input  R,
  input  L,
  input  C,
  output Carry_prime,
  output X7_prime,
  output X6_prime,
  output X5_prime,
  output X4_prime,
  output X3_prime,
  output X2_prime,
  output X1_prime,
  output X0_prime
);

  wire and_1_out, and_2_out, and_3_out, and_4_out, and_5_out, and_6_out, and_7_out, and_8_out, and_9_out,
       and_10_out, and_11_out, and_12_out, and_13_out, and_14_out, and_15_out, and_16_out, and_17_out,
       and_18_out, and_19_out, and_20_out, and_21_out, and_22_out, and_23_out, and_24_out, and_25_out,
       and_26_out, and_27_out, not_1_out, not_2_out;

  not not_1 (not_1_out, R);
  not not_2 (not_2_out, L);
  and and_1 (and_1_out, L, X7);
  and and_2 (and_2_out, not_2_out, Carry, not_1_out);
  or or_1 (Carry_prime, and_27_out, and_2_out, and_1_out);
  and and_3 (and_3_out, C, Carry_prime, R);
  and and_4 (and_4_out, not_2_out, X7, not_1_out);
  and and_5 (and_5_out, X7, R);
  or or_2 (X7_prime, and_3_out, and_4_out, and_7_out);
  and and_6 (and_6_out, not_2_out, X6, not_1_out);
  and and_7 (and_7_out, L, X6);
  or or_3 (X6_prime, and_5_out, and_6_out, and_9_out);
  and and_8 (and_8_out, X6, R);
  and and_9 (and_9_out, L, X5);
  and and_10 (and_10_out, not_2_out, X5, not_1_out);
  and and_11 (and_11_out, X5, R);
  or or_4 (X5_prime, and_8_out, and_10_out, and_12_out);
  and and_12 (and_12_out, L, X4);
  and and_13 (and_13_out, X4, R);
  and and_14 (and_14_out, not_2_out, X4, not_1_out);
  or or_5 (X4_prime, and_11_out, and_14_out, and_15_out);
  and and_15 (and_15_out, L, X3);
  and and_16 (and_16_out, not_2_out, X3, not_1_out);
  or or_6 (X3_prime, and_13_out, and_16_out, and_18_out);
  and and_17 (and_17_out, X3, R);
  and and_18 (and_18_out, L, X2);
  and and_19 (and_19_out, not_2_out, X2, not_1_out);
  and and_20 (and_20_out, X2, R);
  or or_7 (X2_prime, and_17_out, and_19_out, and_21_out);
  and and_21 (and_21_out, L, X1);
  and and_22 (and_22_out, not_2_out, X1, not_1_out);
  or or_8 (X1_prime, and_20_out, and_22_out, and_24_out);
  and and_23 (and_23_out, X1, R);
  and and_24 (and_24_out, L, X0);
  and and_25 (and_25_out, not_2_out, X0, not_1_out);
  and and_26 (and_26_out, C, Carry_prime, L);
  or or_9 (X0_prime, and_23_out, and_25_out, and_26_out);
  and and_27 (and_27_out, X0, R);
endmodule

module Parity (
  input  Odd,
  input  C,
  input  [3:0] X4__7,
  input  [3:0] X0__3,
  output Parity
);

  wire xor_1_out, xor_2_out, xor_3_out, xor_5_out, xor_6_out, xor_7_out, xor_8_out, xor_9_out;

  xor xor_1 (xor_1_out, X4__7[3], X4__7[2]);
  xor xor_2 (xor_2_out, Odd, C);
  xor xor_3 (xor_3_out, xor_1_out, xor_6_out);
  xor xor_4 (Parity, xor_2_out, xor_8_out);
  xor xor_5 (xor_5_out, X0__3[3], X0__3[2]);
  xor xor_6 (xor_6_out, X4__7[1], X4__7[0]);
  xor xor_7 (xor_7_out, xor_5_out, xor_9_out);
  xor xor_8 (xor_8_out, xor_3_out, xor_7_out);
  xor xor_9 (xor_9_out, X0__3[1], X0__3[0]);
endmodule
