// Logisim project 8BITALU.circ as structural Verilog: 4 circuits, main circuit ALU
module ALU (
  input  R,
  input  L,
  input  C,
  input  F2,
  input  F1,
  input  F0,
  input  Cin,
  input  M,
  input  B7,
  input  in_10,
  input  in_11,
  input  in_12,
  input  in_13,
  input  in_14,
  input  in_15,
  input  B0,
  input  A7,
  input  in_18,
  input  in_19,
  input  in_20,
  input  in_21,
  input  in_22,
  input  in_23,
  input  A0,
  output Zero,
  output A_B,
  output Ovfl,
  output Carry,
  output Sign,
  output S7,
  output out_31,
  output out_32,
  output out_33,
  output out_34,
  output out_35,
  output out_36,
  output S0
);

  wire b_xor_m_1_b0_prime, b_xor_m_1_b1_prime, b_xor_m_1_b2_prime, b_xor_m_1_b3_prime, b_xor_m_1_b4_prime,
       b_xor_m_1_b5_prime, b_xor_m_1_b6_prime, b_xor_m_1_b7_prime, b_xor_m_1_m_2, n1bit_1_a_b, n1bit_1_cout,
       n1bit_1_s, n1bit_2_a_b, n1bit_2_cout, n1bit_2_s, n1bit_3_a_b, n1bit_3_cout, n1bit_3_s, n1bit_4_a_b,
       n1bit_4_cout, n1bit_4_s, n1bit_5_a_b, n1bit_5_cout, n1bit_5_s, n1bit_6_a_b, n1bit_6_cout, n1bit_6_s,
       n1bit_7_a_b, n1bit_7_cout, n1bit_7_s, n1bit_8_a_b, n1bit_8_cout, n1bit_8_s, not_1_out, or_1_out,
       shift_1_x7_prime;

  xor xor_1 (Ovfl, n1bit_4_cout, n1bit_3_cout);
  or or_1 (or_1_out, Cin, M);
  _1BIT u_1bit_1 (
    .F2(F2), .F1(F1), .F0(F0), .Cin(n1bit_8_cout), .B(b_xor_m_1_b4_prime), .A(in_20), .A_B(n1bit_1_a_b),
    .Cout(n1bit_1_cout), .S(n1bit_1_s));
  _1BIT u_1bit_2 (
    .F2(F2), .F1(F1), .F0(F0), .Cin(n1bit_1_cout), .B(b_xor_m_1_b5_prime), .A(in_19), .A_B(n1bit_2_a_b),
    .Cout(n1bit_2_cout), .S(n1bit_2_s));
  _1BIT u_1bit_3 (
    .F2(F2), .F1(F1), .F0(F0), .Cin(n1bit_2_cout), .B(b_xor_m_1_b6_prime), .A(in_18), .A_B(n1bit_3_a_b),
    .Cout(n1bit_3_cout), .S(n1bit_3_s));
  _1BIT u_1bit_4 (
    .F2(F2), .F1(F1), .F0(F0), .Cin(n1bit_3_cout), .B(b_xor_m_1_b7_prime), .A(A7), .A_B(n1bit_4_a_b),
    .Cout(n1bit_4_cout), .S(n1bit_4_s));
  and and_1 (A_B, n1bit_8_a_b, n1bit_7_a_b, n1bit_6_a_b, n1bit_5_a_b, n1bit_4_a_b, n1bit_3_a_b, n1bit_2_a_b, n1bit_1_a_b);
  B_XOR_M b_xor_m_1 (
    .M(M), .M_2(b_xor_m_1_m_2), .B7(B7), .B6(in_10), .B5(in_11), .B4(in_12), .B3(in_13), .B2(in_14),
    .B1(in_15), .B0(B0), .B7_prime(b_xor_m_1_b7_prime), .B6_prime(b_xor_m_1_b6_prime),
    .B5_prime(b_xor_m_1_b5_prime), .B4_prime(b_xor_m_1_b4_prime), .B3_prime(b_xor_m_1_b3_prime),
    .B2_prime(b_xor_m_1_b2_prime), .B1_prime(b_xor_m_1_b1_prime), .B0_prime(b_xor_m_1_b0_prime));
  _1BIT u_1bit_5 (
    .F2(F2), .F1(F1), .F0(F0), .Cin(or_1_out), .B(b_xor_m_1_b0_prime), .A(A0), .A_B(n1bit_5_a_b),
    .Cout(n1bit_5_cout), .S(n1bit_5_s));
  _1BIT u_1bit_6 (
    .F2(F2), .F1(F1), .F0(F0), .Cin(n1bit_5_cout), .B(b_xor_m_1_b1_prime), .A(in_23), .A_B(n1bit_6_a_b),
    .Cout(n1bit_6_cout), .S(n1bit_6_s));
  _1BIT u_1bit_7 (
    .F2(F2), .F1(F1), .F0(F0), .Cin(n1bit_6_cout), .B(b_xor_m_1_b2_prime), .A(in_22), .A_B(n1bit_7_a_b),
    .Cout(n1bit_7_cout), .S(n1bit_7_s));
  _1BIT u_1bit_8 (
    .F2(F2), .F1(F1), .F0(F0), .Cin(n1bit_7_cout), .B(b_xor_m_1_b3_prime), .A(in_21), .A_B(n1bit_8_a_b),
    .Cout(n1bit_8_cout), .S(n1bit_8_s));
  nor nor_1 (Zero, n1bit_4_s, n1bit_3_s, n1bit_2_s, n1bit_1_s, n1bit_8_s, n1bit_7_s, n1bit_6_s, n1bit_5_s, n1bit_4_cout);
  and and_2 (Sign, b_xor_m_1_m_2, shift_1_x7_prime);
  not not_1 (not_1_out, b_xor_m_1_m_2);
  and and_3 (S7, not_1_out, shift_1_x7_prime);
  Shift shift_1 (
    .R(R), .L(L), .C(C), .Carry(n1bit_4_cout), .X7(n1bit_4_s), .X6(n1bit_3_s), .X5(n1bit_2_s),
    .X4(n1bit_1_s), .X3(n1bit_8_s), .X2(n1bit_7_s), .X1(n1bit_6_s), .X0(n1bit_5_s), .Carry_prime(Carry),
    .X7_prime(shift_1_x7_prime), .X6_prime(out_31), .X5_prime(out_32), .X4_prime(out_33), .X3_prime(out_34),
    .X2_prime(out_35), .X1_prime(out_36), .X0_prime(S0));
endmodule

module B_XOR_M (
  input  B7,
  input  B6,
  input  B5,
  input  B4,
  input  B3,
  input  B2,
  input  B1,
  input  B0,
  input  M,
  output M_2,
  output B7_prime,
  output B6_prime,
  output B5_prime,
  output B4_prime,
  output B3_prime,
  output B2_prime,
  output B1_prime,
  output B0_prime
);

  xor xor_1 (B6_prime, B6, M);
  xor xor_2 (B7_prime, B7, M);
  xor xor_3 (B5_prime, B5, M);
  xor xor_4 (B4_prime, B4, M);
  xor xor_5 (B2_prime, B2, M);
  xor xor_6 (B3_prime, B3, M);
  xor xor_7 (B0_prime, B0, M);
  xor xor_8 (B1_prime, B1, M);

  assign M_2 = M;
endmodule

module _1BIT (
  input  F2,
  input  F1,
  input  F0,
  input  Cin,
  input  B,
  input  A,
  output A_B,
  output Cout,
  output S
);

  wire and_1_out, and_2_out, and_3_out, and_4_out, and_5_out, and_6_out, and_7_out, and_8_out, and_9_out,
       and_10_out, and_11_out, and_12_out, and_13_out, and_14_out, and_15_out, not_1_out, not_2_out,
       not_3_out, not_4_out, not_5_out, not_6_out;

  not not_1 (not_1_out, F2);
  not not_2 (not_2_out, F1);
  not not_3 (not_3_out, F0);
  not not_4 (not_4_out, Cin);
  not not_5 (not_5_out, B);
  not not_6 (not_6_out, A);
  and and_1 (and_1_out, not_1_out, not_2_out, not_3_out, A, B);
  and and_2 (and_2_out, not_1_out, not_2_out, not_3_out, A, Cin);
  and and_3 (and_3_out, not_1_out, not_2_out, not_3_out, B, Cin);
  and and_4 (and_4_out, not_2_out, not_3_out, not_4_out, not_5_out, A);
  and and_5 (and_5_out, not_2_out, not_3_out, not_4_out, not_6_out, B);
  and and_6 (and_6_out, not_1_out, not_3_out, not_5_out, not_6_out, Cin);
  and and_7 (and_7_out, not_2_out, not_3_out, A, B, Cin);
  and and_8 (and_8_out, not_1_out, not_2_out, A, B, F0);
  and and_9 (and_9_out, not_1_out, not_6_out, F1);
  and and_10 (and_10_out, not_5_out, not_6_out, F1);
  and and_11 (and_11_out, not_1_out, not_5_out, F0, F1);
  and and_12 (and_12_out, not_2_out, not_5_out, A, F2);
  and and_13 (and_13_out, not_2_out, not_3_out, B, F2);
  and and_14 (and_14_out, not_2_out, not_6_out, B, F2);
  and and_15 (and_15_out, A, B, F0, F1, F2);
  xnor xnor_1 (A_B, B, A);
  or or_1 (Cout, and_1_out, and_2_out, and_3_out);
  or or_2 (S, and_4_out, and_5_out, and_6_out, and_7_out, and_8_out, and_9_out, and_10_out, and_11_out, and_12_out, and_13_out, and_14_out, and_15_out);
endmodule

module Shift (
  input  Carry,
  input  X7,
  input  X6,
  input  X5,
  input  X4,
  input  X3,
  input  X2,
  input  X1,
  input  X0,
  input  R,
  input  L,
  input  C,
  output Carry_prime,
  output X7_prime,
  output X6_prime,
  output X5_prime,
  output X4_prime,
  output X3_prime,
  output X2_prime,
  output X1_prime,
  output X0_prime
);

  wire and_1_out, and_2_out, and_3_out, and_4_out, and_5_out, and_6_out, and_7_out, and_8_out, and_9_out,
       and_10_out, and_11_out, and_12_out, and_13_out, and_14_out, and_15_out, and_16_out, and_17_out,
       and_18_out, and_19_out, and_20_out, and_21_out, and_22_out, and_23_out, and_24_out, and_25_out,
       and_26_out, and_27_out, not_1_out, not_2_out;

  not not_1 (not_1_out, R);
  not not_2 (not_2_out, L);
  and and_1 (and_1_out, L, X7);
  and and_2 (and_2_out, not_2_out, Carry, not_1_out);
  or or_1 (Carry_prime, and_27_out, and_2_out, and_1_out);
  and and_3 (and_3_out, C, Carry_prime, R);
  and and_4 (and_4_out, not_2_out, X7, not_1_out);
  and and_5 (and_5_out, X7, R);
  or or_2 (X7_prime, and_3_out, and_4_out, and_7_out);
  and and_6 (and_6_out, not_2_out, X6, not_1_out);
  and and_7 (and_7_out, L, X6);
  or or_3 (X6_prime, and_5_out, and_6_out, and_9_out);
  and and_8 (and_8_out, X6, R);
  and and_9 (and_9_out, L, X5);
  and and_10 (and_10_out, not_2_out, X5, not_1_out);
  and and_11 (and_11_out, X5, R);
  or or_4 (X5_prime, and_8_out, and_10_out, and_12_out);
  and and_12 (and_12_out, L, X4);
  and and_13 (and_13_out, not_2_out, X4, not_1_out);
  and and_14 (and_14_out, X4, R);
  or or_5 (X4_prime, and_11_out, and_13_out, and_16_out);
  and and_15 (and_15_out, not_2_out, X3, not_1_out);
  and and_16 (and_16_out, L, X3);
  or or_6 (X3_prime, and_14_out, and_15_out, and_18_out);
  and and_17 (and_17_out, X3, R);
  and and_18 (and_18_out, L, X2);
  and and_19 (and_19_out, not_2_out, X2, not_1_out);
  and and_20 (and_20_out, X2, R);
  or or_7 (X2_prime, and_17_out, and_19_out, and_22_out);
  and and_21 (and_21_out, not_2_out, X1, not_1_out);
  and and_22 (and_22_out, L, X1);
  or or_8 (X1_prime, and_20_out, and_21_out, and_24_out);
  and and_23 (and_23_out, X1, R);
  and and_24 (and_24_out, L, X0);
  and and_25 (and_25_out, not_2_out, X0, not_1_out);
  and and_26 (and_26_out, C, Carry_prime, L);
  or or_9 (X0_prime, and_23_out, and_25_out, and_26_out);
  and and_27 (and_27_out, X0, R);
endmodule
