// Logisim project 8_Bit_ALU.circ as structural Verilog: 7 circuits, main circuit ALU
module ALU (
  input  ODD,
  input  B7,
  input  in_3,
  input  in_4,
  input  in_5,
  input  in_6,
  input  in_7,
  input  in_8,
  input  B0,
  input  A7,
  input  in_11,
  input  in_12,
  input  in_13,
  input  in_14,
  input  in_15,
  input  in_16,
  input  A0,
  input  LS,
  input  RS,
  input  nX,
  input  Cin,
  input  nAND,
  input  nC,
  input  nB,
  input  nA,
  output X7,
  output out_27,
  output out_28,
  output out_29,
  output out_30,
  output out_31,
  output out_32,
  output X0,
  output OVERFLOW,
  output ZERO,
  output PARITY,
  output SIGN,
  output CARRY,
  output HALF_CARRY,
  output A_B,
  output A_B_2
);

  wire inv_a_b_1_a0_prime, inv_a_b_1_a1_prime, inv_a_b_1_a2_prime, inv_a_b_1_a3_prime, inv_a_b_1_a4_prime,
       inv_a_b_1_a5_prime, inv_a_b_1_a6_prime, inv_a_b_1_a7_prime, inv_a_b_1_b0_prime, inv_a_b_1_b1_prime,
       inv_a_b_1_b2_prime, inv_a_b_1_b3_prime, inv_a_b_1_b4_prime, inv_a_b_1_b5_prime, inv_a_b_1_b6_prime,
       inv_a_b_1_b7_prime, logic_1_c7, logic_1_x0, logic_1_x1, logic_1_x2, logic_1_x3, logic_1_x4,
       logic_1_x5, logic_1_x6, logic_1_x7, shift_1_overflow;
  wire [7:0] inv_out_1_x0_prime;

  STATUS status_1 (
    .SIGN(SIGN), .PARITY(PARITY), .ZERO(ZERO), .OVERFLOW_2(OVERFLOW), .CIN(Cin), .INV_B(nB),
    .X7(inv_out_1_x0_prime[7]), .X6(inv_out_1_x0_prime[6]), .X5(inv_out_1_x0_prime[5]),
    .X4(inv_out_1_x0_prime[4]), .X3(inv_out_1_x0_prime[3]), .X2(inv_out_1_x0_prime[2]),
    .X1(inv_out_1_x0_prime[1]), .X0(inv_out_1_x0_prime[0]), .CARRY(CARRY), .ODD(ODD), .C7(logic_1_c7),
    .OVERFLOW(shift_1_overflow));
  CMP cmp_1 (
    .A_B(A_B), .A_B_2(A_B_2), .A7(A7), .B7(B7), .A6(in_11), .B6(in_3), .A5(in_12), .B5(in_4), .A4(in_13),
    .B4(in_5), .A3(in_14), .B3(in_6), .A2(in_15), .B2(in_7), .A1(in_16), .B1(in_8), .A0(A0), .B0(B0));
  SHIFT shift_1 (
    .LEFT_SHIFT(LS), .RIGHT_SHIFT(RS), .OVERFLOW(shift_1_overflow), .X7_prime_prime(X7),
    .X6_prime_prime(out_27), .X5_prime_prime(out_28), .X4_prime_prime(out_29), .X3_prime_prime(out_30),
    .X2_prime_prime(out_31), .X1_prime_prime(out_32), .X0_prime_prime(X0), .X7_prime(inv_out_1_x0_prime[7]),
    .X6_prime(inv_out_1_x0_prime[6]), .X5_prime(inv_out_1_x0_prime[5]), .X4_prime(inv_out_1_x0_prime[4]),
    .X3_prime(inv_out_1_x0_prime[3]), .X2_prime(inv_out_1_x0_prime[2]), .X1_prime(inv_out_1_x0_prime[1]),
    .X0_prime(inv_out_1_x0_prime[0]));
  INV_OUT inv_out_1 (
    .INV_X(nX), .X7_prime(inv_out_1_x0_prime[7]), .X6_prime(inv_out_1_x0_prime[6]),
    .X5_prime(inv_out_1_x0_prime[5]), .X4_prime(inv_out_1_x0_prime[4]), .X3_prime(inv_out_1_x0_prime[3]),
    .X2_prime(inv_out_1_x0_prime[2]), .X1_prime(inv_out_1_x0_prime[1]), .X0_prime(inv_out_1_x0_prime[0]),
    .X7(logic_1_x7), .X6(logic_1_x6), .X5(logic_1_x5), .X4(logic_1_x4), .X3(logic_1_x3), .X2(logic_1_x2),
    .X1(logic_1_x1), .X0(logic_1_x0));
  LOGIC logic_1 (
    .CARRY_OUT(CARRY), .HALF_CARRY(HALF_CARRY), .CARRY_IN(Cin), .INHIBIT_CARRY(nC), .INHIBIT_AND(nAND),
    .X7(logic_1_x7), .X3(logic_1_x3), .C7(logic_1_c7), .X6(logic_1_x6), .X2(logic_1_x2), .X5(logic_1_x5),
    .X1(logic_1_x1), .X4(logic_1_x4), .X0(logic_1_x0), .A7_prime(inv_a_b_1_a7_prime),
    .A3_prime(inv_a_b_1_a3_prime), .B7_prime(inv_a_b_1_b7_prime), .B3_prime(inv_a_b_1_b3_prime),
    .A6_prime(inv_a_b_1_a6_prime), .A2_prime(inv_a_b_1_a2_prime), .B6_prime(inv_a_b_1_b6_prime),
    .B2_prime(inv_a_b_1_b2_prime), .A5_prime(inv_a_b_1_a5_prime), .A1_prime(inv_a_b_1_a1_prime),
    .B5_prime(inv_a_b_1_b5_prime), .B1_prime(inv_a_b_1_b1_prime), .A4_prime(inv_a_b_1_a4_prime),
    .A0_prime(inv_a_b_1_a0_prime), .B4_prime(inv_a_b_1_b4_prime), .B0_prime(inv_a_b_1_b0_prime));
  INV_A_B inv_a_b_1 (
    .A7_prime(inv_a_b_1_a7_prime), .B7_prime(inv_a_b_1_b7_prime), .A6_prime(inv_a_b_1_a6_prime),
    .B6_prime(inv_a_b_1_b6_prime), .A5_prime(inv_a_b_1_a5_prime), .B5_prime(inv_a_b_1_b5_prime),
    .A4_prime(inv_a_b_1_a4_prime), .B4_prime(inv_a_b_1_b4_prime), .A3_prime(inv_a_b_1_a3_prime),
    .B3_prime(inv_a_b_1_b3_prime), .A2_prime(inv_a_b_1_a2_prime), .B2_prime(inv_a_b_1_b2_prime),
    .A1_prime(inv_a_b_1_a1_prime), .B1_prime(inv_a_b_1_b1_prime), .A0_prime(inv_a_b_1_a0_prime),
    .B0_prime(inv_a_b_1_b0_prime), .A7(B7), .B7(A7), .A6(in_3), .B6(in_11), .A5(in_4), .B5(in_12), .A4(in_5),
    .B4(in_13), .A3(in_6), .B3(in_14), .A2(in_7), .B2(in_15), .A1(in_8), .B1(in_16), .A0(B0), .B0(A0),
    .INV_A(nB), .INV_B(nA));

  // Notes on the sheet:
  //   8 BIT ALU
  //   0000 0000 :: ADD
  //   0001 0000 :: INC
  //   0001 0010 :: SUB
  //   0010 1011 :: AND
  //   0000 1011 :: NAND
  //   0000 1000 :: OR
  //   0010 1000 :: NOR
  //   0000 0100 :: XOR
  //   0010 0100 :: XNOR
  //   0010 0000 :: NOT
  //   0000 0001 :: NOT A
  //   0000 0010 :: NOT B
  //   1000 0000 :: LSL
  //   0100 0000 :: LSR
endmodule

module STATUS (
  input  CIN,
  input  INV_B,
  input  X7,
  input  X6,
  input  X5,
  input  X4,
  input  X3,
  input  X2,
  input  X1,
  input  X0,
  input  CARRY,
  input  ODD,
  input  C7,
  input  OVERFLOW,
  output SIGN,
  output PARITY,
  output ZERO,
  output OVERFLOW_2
);

  wire and_2_out, and_3_out, and_4_out, and_6_out, and_7_out, and_8_out, and_9_out, and_10_out, and_11_out,
       and_12_out, nand_1_out, nand_2_out, nand_3_out, nand_4_out, nand_5_out, nand_6_out, nand_7_out,
       nand_8_out, nand_9_out, nand_10_out, or_1_out, or_2_out, or_3_out, or_4_out, or_5_out, or_6_out,
       or_7_out, or_8_out, or_9_out, or_10_out, or_11_out, or_12_out, or_13_out, or_14_out;

  and and_1 (SIGN, CIN, and_2_out);
  and and_2 (and_2_out, INV_B, X7);
  nand nand_1 (nand_1_out, and_3_out, and_9_out);
  and and_3 (and_3_out, nand_2_out, or_4_out);
  nand nand_2 (nand_2_out, and_4_out, and_7_out);
  and and_4 (and_4_out, nand_3_out, or_1_out);
  nand nand_3 (nand_3_out, X7, X6);
  or or_1 (or_1_out, X7, X6);
  and and_5 (PARITY, nand_4_out, or_2_out);
  nand nand_4 (nand_4_out, and_6_out, and_11_out);
  or or_2 (or_2_out, and_6_out, and_11_out);
  and and_6 (and_6_out, nand_1_out, or_3_out);
  or or_3 (or_3_out, and_3_out, and_9_out);
  or or_4 (or_4_out, and_4_out, and_7_out);
  or or_5 (or_5_out, or_1_out, or_6_out);
  or or_6 (or_6_out, X5, X4);
  or or_7 (or_7_out, or_5_out, or_9_out);
  and and_7 (and_7_out, or_6_out, nand_5_out);
  nand nand_5 (nand_5_out, X5, X4);
  nand nand_6 (nand_6_out, X3, X2);
  or or_8 (or_8_out, and_8_out, and_10_out);
  and and_8 (and_8_out, nand_6_out, or_10_out);
  or or_9 (or_9_out, or_10_out, or_12_out);
  or or_10 (or_10_out, X3, X2);
  not not_1 (ZERO, or_11_out);
  or or_11 (or_11_out, or_7_out, CARRY);
  and and_9 (and_9_out, or_8_out, nand_7_out);
  nand nand_7 (nand_7_out, and_8_out, and_10_out);
  and and_10 (and_10_out, or_12_out, nand_8_out);
  nand nand_8 (nand_8_out, X1, X0);
  or or_12 (or_12_out, X1, X0);
  and and_11 (and_11_out, or_13_out, nand_9_out);
  nand nand_9 (nand_9_out, CARRY, ODD);
  or or_13 (or_13_out, CARRY, ODD);
  and and_12 (and_12_out, or_14_out, nand_10_out);
  or or_14 (or_14_out, CARRY, C7);
  or or_15 (OVERFLOW_2, and_12_out, OVERFLOW);
  nand nand_10 (nand_10_out, CARRY, C7);
endmodule

module SHIFT (
  input  LEFT_SHIFT,
  input  RIGHT_SHIFT,
  input  X7_prime,
  input  X6_prime,
  input  X5_prime,
  input  X4_prime,
  input  X3_prime,
  input  X2_prime,
  input  X1_prime,
  input  X0_prime,
  output OVERFLOW,
  output X7_prime_prime,
  output X6_prime_prime,
  output X5_prime_prime,
  output X4_prime_prime,
  output X3_prime_prime,
  output X2_prime_prime,
  output X1_prime_prime,
  output X0_prime_prime
);

  wire and_2_out, and_3_out, and_4_out, and_5_out, and_6_out, and_7_out, and_8_out, and_9_out, and_10_out,
       and_11_out, and_12_out, and_13_out, and_14_out, and_15_out, and_16_out, and_17_out, and_18_out,
       and_19_out, and_20_out, and_21_out, and_22_out, and_23_out, not_1_out, or_3_out, or_5_out, or_7_out,
       or_9_out, or_11_out, or_13_out, or_15_out;

  or or_1 (X7_prime_prime, and_2_out, and_4_out);
  and and_1 (OVERFLOW, X7_prime, LEFT_SHIFT);
  and and_2 (and_2_out, X7_prime, not_1_out);
  and and_3 (and_3_out, X7_prime, RIGHT_SHIFT);
  and and_4 (and_4_out, X6_prime, LEFT_SHIFT);
  or or_2 (X6_prime_prime, or_3_out, and_7_out);
  or or_3 (or_3_out, and_3_out, and_5_out);
  and and_5 (and_5_out, X6_prime, not_1_out);
  and and_6 (and_6_out, X6_prime, RIGHT_SHIFT);
  or or_4 (X5_prime_prime, or_5_out, and_11_out);
  or or_5 (or_5_out, and_6_out, and_8_out);
  and and_7 (and_7_out, X5_prime, LEFT_SHIFT);
  and and_8 (and_8_out, X5_prime, not_1_out);
  and and_9 (and_9_out, X5_prime, RIGHT_SHIFT);
  or or_6 (X4_prime_prime, or_7_out, and_13_out);
  or or_7 (or_7_out, and_9_out, and_10_out);
  and and_10 (and_10_out, X4_prime, not_1_out);
  and and_11 (and_11_out, X4_prime, LEFT_SHIFT);
  and and_12 (and_12_out, X4_prime, RIGHT_SHIFT);
  and and_13 (and_13_out, X3_prime, LEFT_SHIFT);
  or or_8 (X3_prime_prime, or_9_out, and_16_out);
  or or_9 (or_9_out, and_12_out, and_14_out);
  and and_14 (and_14_out, X3_prime, not_1_out);
  and and_15 (and_15_out, X3_prime, RIGHT_SHIFT);
  or or_10 (X2_prime_prime, or_11_out, and_18_out);
  or or_11 (or_11_out, and_15_out, and_17_out);
  and and_16 (and_16_out, X2_prime, LEFT_SHIFT);
  and and_17 (and_17_out, X2_prime, not_1_out);
  and and_18 (and_18_out, X1_prime, LEFT_SHIFT);
  and and_19 (and_19_out, X2_prime, RIGHT_SHIFT);
  or or_12 (X1_prime_prime, or_13_out, and_21_out);
  or or_13 (or_13_out, and_19_out, and_20_out);
  and and_20 (and_20_out, X1_prime, not_1_out);
  or or_14 (X0_prime_prime, and_22_out, and_23_out);
  and and_21 (and_21_out, X0_prime, LEFT_SHIFT);
  and and_22 (and_22_out, X1_prime, RIGHT_SHIFT);
  and and_23 (and_23_out, X0_prime, not_1_out);
  not not_1 (not_1_out, or_15_out);
  or or_15 (or_15_out, RIGHT_SHIFT, LEFT_SHIFT);
endmodule

module INV_OUT (
  input  INV_X,
  input  X7,
  input  X6,
  input  X5,
  input  X4,
  input  X3,
  input  X2,
  input  X1,
  input  X0,
  output X7_prime,
  output X6_prime,
  output X5_prime,
  output X4_prime,
  output X3_prime,
  output X2_prime,
  output X1_prime,
  output X0_prime
);

  wire nand_1_out, nand_2_out, nand_3_out, nand_4_out, nand_5_out, nand_6_out, nand_7_out, nand_8_out,
       or_1_out, or_2_out, or_3_out, or_4_out, or_5_out, or_6_out, or_7_out, or_8_out;

  nand nand_1 (nand_1_out, X7, INV_X);
  and and_1 (X7_prime, nand_1_out, or_1_out);
  or or_1 (or_1_out, X7, INV_X);
  and and_2 (X6_prime, nand_2_out, or_2_out);
  nand nand_2 (nand_2_out, X6, INV_X);
  or or_2 (or_2_out, X6, INV_X);
  and and_3 (X5_prime, nand_3_out, or_3_out);
  nand nand_3 (nand_3_out, X5, INV_X);
  or or_3 (or_3_out, X5, INV_X);
  and and_4 (X4_prime, nand_4_out, or_4_out);
  nand nand_4 (nand_4_out, X4, INV_X);
  or or_4 (or_4_out, X4, INV_X);
  and and_5 (X3_prime, nand_5_out, or_5_out);
  nand nand_5 (nand_5_out, X3, INV_X);
  or or_5 (or_5_out, X3, INV_X);
  and and_6 (X2_prime, nand_6_out, or_6_out);
  nand nand_6 (nand_6_out, X2, INV_X);
  and and_7 (X1_prime, nand_7_out, or_7_out);
  nand nand_7 (nand_7_out, X1, INV_X);
  or or_6 (or_6_out, X2, INV_X);
  and and_8 (X0_prime, nand_8_out, or_8_out);
  nand nand_8 (nand_8_out, X0, INV_X);
  or or_7 (or_7_out, X1, INV_X);
  or or_8 (or_8_out, X0, INV_X);
endmodule

module LOGIC (
  input  A7_prime,
  input  A6_prime,
  input  A5_prime,
  input  A4_prime,
  input  B7_prime,
  input  B6_prime,
  input  B5_prime,
  input  B4_prime,
  input  CARRY_IN,
  input  INHIBIT_CARRY,
  input  INHIBIT_AND,
  input  A3_prime,
  input  A2_prime,
  input  A1_prime,
  input  A0_prime,
  input  B3_prime,
  input  B2_prime,
  input  B1_prime,
  input  B0_prime,
  output X7,
  output C7,
  output X6,
  output X5,
  output X4,
  output CARRY_OUT,
  output X3,
  output X2,
  output X1,
  output X0,
  output HALF_CARRY
);

  wire and_4_out, and_5_out, and_6_out, and_8_out, and_9_out, and_10_out, and_11_out, and_12_out, and_14_out,
       and_16_out, and_17_out, and_18_out, and_20_out, and_21_out, and_22_out, and_23_out, and_24_out,
       and_26_out, and_28_out, and_29_out, and_30_out, and_31_out, and_32_out, and_33_out, and_34_out,
       and_35_out, and_36_out, and_37_out, and_38_out, and_40_out, and_41_out, and_42_out, and_44_out,
       and_45_out, and_46_out, and_47_out, and_48_out, not_1_out, not_2_out, not_3_out, not_4_out, not_5_out,
       not_6_out, not_7_out, not_8_out, not_9_out, not_10_out, not_11_out, not_12_out, not_13_out,
       not_14_out, not_15_out, not_16_out, not_17_out, not_18_out, or_1_out, or_2_out, or_3_out, or_4_out,
       or_5_out, or_6_out, or_7_out, or_8_out, or_9_out, or_10_out, or_11_out, or_12_out, or_13_out,
       or_14_out, or_15_out, or_16_out, or_17_out, or_18_out, or_19_out, or_20_out, or_21_out, or_22_out,
       or_23_out, or_24_out;

  and and_1 (CARRY_OUT, not_17_out, or_2_out);
  and and_2 (HALF_CARRY, not_17_out, or_3_out);
  and and_3 (X7, not_1_out, or_1_out);
  not not_1 (not_1_out, and_4_out);
  or or_1 (or_1_out, C7, and_9_out);
  and and_4 (and_4_out, and_9_out, C7);
  and and_5 (and_5_out, not_18_out, and_6_out);
  or or_2 (or_2_out, and_4_out, and_5_out);
  and and_6 (and_6_out, A7_prime, B7_prime);
  and and_7 (X3, not_2_out, or_5_out);
  not not_2 (not_2_out, and_10_out);
  and and_8 (and_8_out, not_18_out, and_12_out);
  or or_3 (or_3_out, and_10_out, and_8_out);
  and and_9 (and_9_out, not_3_out, or_4_out);
  not not_3 (not_3_out, and_5_out);
  or or_4 (or_4_out, A7_prime, B7_prime);
  or or_5 (or_5_out, and_14_out, and_11_out);
  and and_10 (and_10_out, and_11_out, and_14_out);
  and and_11 (and_11_out, not_4_out, or_6_out);
  not not_4 (not_4_out, and_8_out);
  or or_6 (or_6_out, A3_prime, B3_prime);
  and and_12 (and_12_out, A3_prime, B3_prime);
  and and_13 (C7, not_17_out, or_7_out);
  or or_7 (or_7_out, and_16_out, and_17_out);
  and and_14 (and_14_out, not_17_out, or_10_out);
  and and_15 (X6, not_5_out, or_8_out);
  or or_8 (or_8_out, and_26_out, and_23_out);
  not not_5 (not_5_out, and_16_out);
  and and_16 (and_16_out, and_23_out, and_26_out);
  and and_17 (and_17_out, not_18_out, and_18_out);
  not not_6 (not_6_out, and_17_out);
  and and_18 (and_18_out, A6_prime, B6_prime);
  and and_19 (X2, not_7_out, or_9_out);
  not not_7 (not_7_out, and_20_out);
  or or_9 (or_9_out, and_28_out, and_24_out);
  and and_20 (and_20_out, and_24_out, and_28_out);
  and and_21 (and_21_out, not_18_out, and_22_out);
  not not_8 (not_8_out, and_21_out);
  or or_10 (or_10_out, and_20_out, and_21_out);
  and and_22 (and_22_out, A2_prime, B2_prime);
  and and_23 (and_23_out, not_6_out, or_11_out);
  or or_11 (or_11_out, A6_prime, B6_prime);
  and and_24 (and_24_out, not_8_out, or_12_out);
  or or_12 (or_12_out, A2_prime, B2_prime);
  and and_25 (X5, not_9_out, or_15_out);
  not not_9 (not_9_out, and_29_out);
  and and_26 (and_26_out, not_17_out, or_13_out);
  or or_13 (or_13_out, and_29_out, and_31_out);
  and and_27 (X1, not_10_out, or_17_out);
  not not_10 (not_10_out, and_33_out);
  and and_28 (and_28_out, not_17_out, or_14_out);
  or or_14 (or_14_out, and_33_out, and_35_out);
  or or_15 (or_15_out, and_37_out, and_30_out);
  and and_29 (and_29_out, and_30_out, and_37_out);
  and and_30 (and_30_out, not_11_out, or_16_out);
  and and_31 (and_31_out, not_18_out, and_32_out);
  not not_11 (not_11_out, and_31_out);
  or or_16 (or_16_out, A5_prime, B5_prime);
  and and_32 (and_32_out, A5_prime, B5_prime);
  or or_17 (or_17_out, and_38_out, and_34_out);
  and and_33 (and_33_out, and_34_out, and_38_out);
  and and_34 (and_34_out, not_12_out, or_18_out);
  and and_35 (and_35_out, not_18_out, and_36_out);
  not not_12 (not_12_out, and_35_out);
  and and_36 (and_36_out, A1_prime, B1_prime);
  and and_37 (and_37_out, not_17_out, or_20_out);
  and and_38 (and_38_out, not_17_out, or_22_out);
  or or_18 (or_18_out, A1_prime, B1_prime);
  and and_39 (X4, not_13_out, or_19_out);
  not not_13 (not_13_out, and_40_out);
  or or_19 (or_19_out, HALF_CARRY, and_47_out);
  and and_40 (and_40_out, and_47_out, HALF_CARRY);
  and and_41 (and_41_out, not_18_out, and_42_out);
  or or_20 (or_20_out, and_40_out, and_41_out);
  and and_42 (and_42_out, A4_prime, B4_prime);
  and and_43 (X0, not_14_out, or_21_out);
  not not_14 (not_14_out, and_44_out);
  or or_21 (or_21_out, CARRY_IN, and_48_out);
  and and_44 (and_44_out, and_48_out, CARRY_IN);
  and and_45 (and_45_out, not_18_out, and_46_out);
  or or_22 (or_22_out, and_44_out, and_45_out);
  and and_46 (and_46_out, A0_prime, B0_prime);
  and and_47 (and_47_out, not_15_out, or_23_out);
  not not_15 (not_15_out, and_41_out);
  or or_23 (or_23_out, A4_prime, B4_prime);
  and and_48 (and_48_out, not_16_out, or_24_out);
  not not_16 (not_16_out, and_45_out);
  or or_24 (or_24_out, A0_prime, B0_prime);
  not not_17 (not_17_out, INHIBIT_CARRY);
  not not_18 (not_18_out, INHIBIT_AND);
endmodule

module INV_A_B (
  input  INV_A,
  input  INV_B,
  input  A7,
  input  A6,
  input  A5,
  input  A4,
  input  A3,
  input  A2,
  input  A1,
  input  A0,
  input  B7,
  input  B6,
  input  B5,
  input  B4,
  input  B3,
  input  B2,
  input  B1,
  input  B0,
  output A7_prime,
  output A6_prime,
  output A5_prime,
  output A4_prime,
  output A3_prime,
  output A2_prime,
  output A1_prime,
  output A0_prime,
  output B7_prime,
  output B6_prime,
  output B5_prime,
  output B4_prime,
  output B3_prime,
  output B2_prime,
  output B1_prime,
  output B0_prime
);

  wire nand_1_out, nand_2_out, nand_3_out, nand_4_out, nand_5_out, nand_6_out, nand_7_out, nand_8_out,
       nand_9_out, nand_10_out, nand_11_out, nand_12_out, nand_13_out, nand_14_out, nand_15_out, nand_16_out,
       or_1_out, or_2_out, or_3_out, or_4_out, or_5_out, or_6_out, or_7_out, or_8_out, or_9_out, or_10_out,
       or_11_out, or_12_out, or_13_out, or_14_out, or_15_out, or_16_out;

  nand nand_1 (nand_1_out, A7, INV_A);
  and and_1 (A7_prime, nand_1_out, or_1_out);
  nand nand_2 (nand_2_out, B7, INV_B);
  or or_1 (or_1_out, A7, INV_A);
  and and_2 (B7_prime, nand_2_out, or_2_out);
  or or_2 (or_2_out, B7, INV_B);
  and and_3 (A6_prime, nand_3_out, or_3_out);
  nand nand_3 (nand_3_out, A6, INV_A);
  or or_3 (or_3_out, A6, INV_A);
  and and_4 (B6_prime, nand_4_out, or_4_out);
  nand nand_4 (nand_4_out, B6, INV_B);
  or or_4 (or_4_out, B6, INV_B);
  and and_5 (A5_prime, nand_5_out, or_5_out);
  nand nand_5 (nand_5_out, A5, INV_A);
  or or_5 (or_5_out, A5, INV_A);
  and and_6 (B5_prime, nand_6_out, or_6_out);
  nand nand_6 (nand_6_out, B5, INV_B);
  or or_6 (or_6_out, B5, INV_B);
  and and_7 (A4_prime, nand_7_out, or_7_out);
  nand nand_7 (nand_7_out, A4, INV_A);
  or or_7 (or_7_out, A4, INV_A);
  and and_8 (B4_prime, nand_8_out, or_8_out);
  nand nand_8 (nand_8_out, B4, INV_B);
  or or_8 (or_8_out, B4, INV_B);
  and and_9 (A3_prime, nand_9_out, or_9_out);
  nand nand_9 (nand_9_out, A3, INV_A);
  or or_9 (or_9_out, A3, INV_A);
  and and_10 (B3_prime, nand_10_out, or_10_out);
  nand nand_10 (nand_10_out, B3, INV_B);
  or or_10 (or_10_out, B3, INV_B);
  and and_11 (A2_prime, nand_11_out, or_11_out);
  nand nand_11 (nand_11_out, A2, INV_A);
  and and_12 (B2_prime, nand_12_out, or_12_out);
  nand nand_12 (nand_12_out, B2, INV_B);
  or or_11 (or_11_out, A2, INV_A);
  and and_13 (A1_prime, nand_13_out, or_13_out);
  nand nand_13 (nand_13_out, A1, INV_A);
  or or_12 (or_12_out, B2, INV_B);
  and and_14 (B1_prime, nand_14_out, or_14_out);
  nand nand_14 (nand_14_out, B1, INV_B);
  or or_13 (or_13_out, A1, INV_A);
  and and_15 (A0_prime, nand_15_out, or_15_out);
  nand nand_15 (nand_15_out, A0, INV_A);
  or or_14 (or_14_out, B1, INV_B);
  and and_16 (B0_prime, nand_16_out, or_16_out);
  nand nand_16 (nand_16_out, B0, INV_B);
  or or_15 (or_15_out, A0, INV_A);
  or or_16 (or_16_out, B0, INV_B);
endmodule

module CMP (
  input  A7,
  input  A6,
  input  A5,
  input  A4,
  input  A3,
  input  A2,
  input  A1,
  input  A0,
  input  B7,
  input  B6,
  input  B5,
  input  B4,
  input  B3,
  input  B2,
  input  B1,
  input  B0,
  output A_B,
  output A_B_2
);

  wire and_1_out, and_2_out, and_3_out, and_4_out, and_5_out, and_6_out, and_7_out, and_8_out, and_9_out,
       and_10_out, and_11_out, and_12_out, and_13_out, and_14_out, and_15_out, and_16_out, and_17_out,
       and_18_out, and_19_out, and_20_out, and_21_out, and_22_out, and_23_out, and_24_out, and_25_out,
       and_26_out, and_27_out, and_28_out, and_29_out, nand_1_out, nand_2_out, nand_3_out, nand_4_out,
       nand_5_out, nand_6_out, nand_7_out, nand_8_out, not_1_out, not_2_out, not_3_out, not_4_out, not_5_out,
       not_6_out, not_7_out, not_8_out, or_1_out, or_2_out, or_3_out, or_4_out, or_5_out, or_6_out, or_7_out,
       or_8_out, or_9_out, or_10_out, or_11_out, or_12_out, or_13_out, or_14_out;

  and and_1 (and_1_out, A7, and_2_out);
  and and_2 (and_2_out, nand_1_out, or_1_out);
  not not_1 (not_1_out, and_2_out);
  or or_1 (or_1_out, A7, B7);
  nand nand_1 (nand_1_out, A7, B7);
  and and_3 (and_3_out, nand_2_out, or_3_out);
  and and_4 (and_4_out, A6, not_1_out);
  not not_2 (not_2_out, and_3_out);
  or or_2 (or_2_out, and_1_out, and_5_out);
  and and_5 (and_5_out, and_4_out, and_3_out);
  and and_6 (and_6_out, not_2_out, not_1_out);
  nand nand_2 (nand_2_out, A6, B6);
  or or_3 (or_3_out, A6, B6);
  and and_7 (and_7_out, A5, and_6_out);
  not not_3 (not_3_out, and_9_out);
  and and_8 (and_8_out, and_7_out, and_9_out);
  and and_9 (and_9_out, nand_3_out, or_4_out);
  and and_10 (and_10_out, not_3_out, and_6_out);
  nand nand_3 (nand_3_out, A5, B5);
  or or_4 (or_4_out, A5, B5);
  or or_5 (or_5_out, or_2_out, and_8_out);
  and and_11 (and_11_out, A4, and_10_out);
  and and_12 (and_12_out, and_11_out, and_13_out);
  and and_13 (and_13_out, nand_4_out, or_6_out);
  not not_4 (not_4_out, and_13_out);
  and and_14 (and_14_out, not_4_out, and_10_out);
  or or_6 (or_6_out, A4, B4);
  or or_7 (or_7_out, or_5_out, and_12_out);
  and and_15 (and_15_out, A3, and_14_out);
  nand nand_4 (nand_4_out, A4, B4);
  and and_16 (and_16_out, and_15_out, and_17_out);
  and and_17 (and_17_out, nand_5_out, or_8_out);
  not not_5 (not_5_out, and_17_out);
  and and_18 (and_18_out, not_5_out, and_14_out);
  or or_8 (or_8_out, A3, B3);
  or or_9 (or_9_out, or_7_out, and_16_out);
  nand nand_5 (nand_5_out, A3, B3);
  and and_19 (and_19_out, nand_6_out, or_11_out);
  and and_20 (and_20_out, A2, and_18_out);
  not not_6 (not_6_out, and_19_out);
  or or_10 (or_10_out, or_9_out, and_21_out);
  and and_21 (and_21_out, and_20_out, and_19_out);
  and and_22 (and_22_out, not_6_out, and_18_out);
  nand nand_6 (nand_6_out, A2, B2);
  or or_11 (or_11_out, A2, B2);
  and and_23 (and_23_out, A1, and_22_out);
  not not_7 (not_7_out, and_25_out);
  and and_24 (and_24_out, and_23_out, and_25_out);
  and and_25 (and_25_out, nand_7_out, or_12_out);
  and and_26 (and_26_out, not_7_out, and_22_out);
  nand nand_7 (nand_7_out, A1, B1);
  or or_12 (or_12_out, A1, B1);
  or or_13 (or_13_out, or_10_out, and_24_out);
  and and_27 (and_27_out, A0, and_26_out);
  and and_28 (and_28_out, and_27_out, and_29_out);
  and and_29 (and_29_out, nand_8_out, or_14_out);
  not not_8 (not_8_out, and_29_out);
  and and_30 (A_B_2, not_8_out, and_26_out);
  or or_14 (or_14_out, A0, B0);
  or or_15 (A_B, or_13_out, and_28_out);
  nand nand_8 (nand_8_out, A0, B0);
endmodule
