// Logisim project 8_Bit_ALU_full.circ as structural Verilog: 1 circuit, main circuit 8_Bit_ALU
module _8_Bit_ALU (
  input  Shift_Left,
  input  Shift_Right,
  input  Invert_Output,
  input  Carry_In,
  input  Inhibit_And,
  input  Inhibit_Carry,
  input  Invert_B,
  input  Invert_A,
  input  A128,
  input  B128,
  input  A64,
  input  B64,
  input  A32,
  input  B32,
  input  A16,
  input  B16,
  input  A8,
  input  B8,
  input  A4,
  input  B4,
  input  A2,
  input  B2,
  input  A1,
  input  B1,
  output _128,
  output _64,
  output _32,
  output _16,
  output _8,
  output _4,
  output _2,
  output _1,
  output Zero,
  output Sign,
  output Carry___V,
  output Half_Carry,
  output A_B,
  output A_B_2
);

  wire and_1_out, and_2_out, and_3_out, and_4_out, and_5_out, and_6_out, and_7_out, and_8_out, and_9_out,
       and_10_out, and_11_out, and_12_out, and_13_out, and_14_out, and_15_out, and_16_out, and_17_out,
       and_18_out, and_19_out, and_20_out, and_21_out, and_22_out, and_23_out, and_24_out, and_25_out,
       and_26_out, and_27_out, and_28_out, and_29_out, and_30_out, and_31_out, and_32_out, and_33_out,
       and_34_out, and_35_out, and_36_out, and_37_out, and_38_out, and_39_out, and_40_out, and_41_out,
       and_42_out, and_43_out, and_44_out, and_45_out, and_46_out, and_47_out, and_48_out, and_49_out,
       and_50_out, and_51_out, and_52_out, and_53_out, and_54_out, and_55_out, and_56_out, and_57_out,
       and_58_out, and_59_out, and_61_out, and_62_out, and_63_out, and_64_out, and_65_out, and_66_out,
       and_67_out, and_68_out, and_69_out, and_70_out, and_71_out, and_72_out, and_73_out, and_74_out,
       and_75_out, and_76_out, and_77_out, and_78_out, and_79_out, and_80_out, and_81_out, and_82_out,
       and_83_out, and_84_out, and_85_out, and_86_out, and_87_out, and_88_out, and_89_out, and_90_out,
       and_91_out, and_92_out, and_93_out, and_94_out, and_95_out, and_96_out, and_97_out, and_98_out,
       and_99_out, and_100_out, and_101_out, and_102_out, and_103_out, and_104_out, and_105_out, and_106_out,
       and_108_out, and_109_out, and_110_out, nand_1_out, nand_2_out, nand_3_out, nand_4_out, nand_5_out,
       nand_6_out, nand_7_out, nand_8_out, nand_9_out, nand_10_out, nand_11_out, nand_12_out, nand_13_out,
       nand_14_out, nand_15_out, nand_16_out, nand_17_out, nand_18_out, nand_19_out, nand_20_out,
       nand_21_out, nand_22_out, nand_23_out, nand_24_out, nand_25_out, nand_26_out, nand_27_out,
       nand_28_out, nand_29_out, nand_30_out, nand_31_out, nand_32_out, not_2_out, not_3_out, not_4_out,
       not_5_out, not_6_out, or_2_out, or_3_out, or_4_out, or_5_out, or_6_out, or_7_out, or_8_out, or_10_out,
       or_11_out, or_12_out, or_13_out, or_14_out, or_15_out, or_17_out, or_18_out, or_19_out, or_20_out,
       or_21_out, or_22_out, or_23_out, or_24_out, or_25_out, or_26_out, or_27_out, or_29_out, or_30_out,
       or_31_out, or_32_out, or_34_out, or_35_out, or_36_out, or_37_out, or_38_out, or_39_out, or_40_out,
       or_41_out, or_42_out, or_43_out, or_44_out, or_45_out, or_47_out, or_48_out, or_49_out, or_50_out,
       or_51_out, or_52_out, or_53_out, or_54_out, or_55_out, or_56_out, or_57_out, or_59_out, or_60_out,
       or_61_out, or_62_out, or_63_out, or_64_out, or_66_out, or_67_out, or_68_out, or_69_out, or_70_out,
       or_71_out, or_72_out, or_73_out, or_74_out, or_76_out, or_78_out, or_79_out;

  and and_1 (and_1_out, Shift_Left, and_7_out);
  and and_2 (and_2_out, ~and_8_out, or_4_out);  // AND_Gate
  and and_3 (and_3_out, not_6_out, or_5_out);
  or or_1 (Carry___V, and_1_out, and_3_out);
  nand nand_1 (nand_1_out, Invert_A, A128);
  and and_4 (and_4_out, nand_4_out, or_8_out);
  and and_5 (and_5_out, not_4_out, not_3_out, and_7_out);
  and and_6 (and_6_out, and_7_out, Shift_Right);
  not not_1 (Zero, or_2_out);
  or or_2 (or_2_out, and_7_out, or_17_out);
  and and_7 (and_7_out, or_3_out, nand_2_out);
  nand nand_2 (nand_2_out, Invert_Output, and_2_out);
  or or_3 (or_3_out, Invert_Output, and_2_out);
  or or_4 (or_4_out, and_9_out, and_18_out);
  and and_8 (and_8_out, and_9_out, and_18_out);
  and and_9 (and_9_out, ~and_10_out, or_6_out);  // AND_Gate
  and and_10 (and_10_out, and_12_out, not_5_out, and_11_out);
  or or_5 (or_5_out, and_8_out, and_10_out);
  or or_6 (or_6_out, and_12_out, and_11_out);
  and and_11 (and_11_out, nand_3_out, or_14_out);
  and and_12 (and_12_out, nand_1_out, or_7_out);
  or or_7 (or_7_out, A128, Invert_A);
  nand nand_3 (nand_3_out, Invert_B, B128);
  and and_13 (and_13_out, A128, and_4_out);
  not not_2 (not_2_out, and_4_out);
  nand nand_4 (nand_4_out, A128, B128);
  or or_8 (or_8_out, A128, B128);
  or or_9 (_128, and_5_out, and_15_out);
  and and_14 (and_14_out, not_4_out, not_3_out, and_24_out);
  and and_15 (and_15_out, Shift_Left, and_24_out);
  nand nand_5 (nand_5_out, Invert_Output, and_16_out);
  or or_10 (or_10_out, Invert_Output, and_16_out);
  and and_16 (and_16_out, ~and_17_out, or_11_out);  // AND_Gate
  or or_11 (or_11_out, and_26_out, and_32_out);
  and and_17 (and_17_out, and_26_out, and_32_out);
  or or_12 (or_12_out, and_17_out, and_27_out);
  and and_18 (and_18_out, not_6_out, or_12_out);
  and and_19 (and_19_out, nand_6_out, or_13_out);
  or or_13 (or_13_out, A64, Invert_A);
  or or_14 (or_14_out, B128, Invert_B);
  nand nand_6 (nand_6_out, Invert_A, A64);
  and and_20 (and_20_out, A64, not_2_out, and_21_out);
  and and_21 (and_21_out, nand_8_out, or_15_out);
  and and_22 (and_22_out, ~and_21_out, not_2_out);  // AND_Gate
  or or_15 (or_15_out, A64, B64);
  or or_16 (_64, and_6_out, and_14_out, and_29_out);
  and and_23 (and_23_out, and_24_out, Shift_Right);
  or or_17 (or_17_out, and_24_out, or_21_out);
  and and_24 (and_24_out, or_10_out, nand_5_out);
  and and_25 (and_25_out, ~and_31_out, or_23_out);  // AND_Gate
  and and_26 (and_26_out, ~and_27_out, or_18_out);  // AND_Gate
  or or_18 (or_18_out, and_19_out, and_28_out);
  and and_27 (and_27_out, and_19_out, not_5_out, and_28_out);
  and and_28 (and_28_out, nand_7_out, or_19_out);
  or or_19 (or_19_out, B64, Invert_B);
  nand nand_7 (nand_7_out, Invert_B, B64);
  or or_20 (or_20_out, and_13_out, and_20_out);
  nand nand_8 (nand_8_out, A64, B64);
  and and_29 (and_29_out, Shift_Left, and_40_out);
  and and_30 (and_30_out, not_4_out, not_3_out, and_40_out);
  or or_21 (or_21_out, and_40_out, or_34_out);
  or or_22 (or_22_out, Invert_Output, and_25_out);
  nand nand_9 (nand_9_out, Invert_Output, and_25_out);
  or or_23 (or_23_out, and_43_out, and_44_out);
  and and_31 (and_31_out, and_43_out, and_44_out);
  and and_32 (and_32_out, not_6_out, or_24_out);
  or or_24 (or_24_out, and_31_out, and_33_out);
  and and_33 (and_33_out, and_34_out, not_5_out, and_45_out);
  and and_34 (and_34_out, nand_10_out, or_25_out);
  or or_25 (or_25_out, A32, Invert_A);
  nand nand_10 (nand_10_out, Invert_A, A32);
  nand nand_11 (nand_11_out, Invert_B, B32);
  or or_26 (or_26_out, or_20_out, and_35_out);
  and and_35 (and_35_out, A32, and_22_out, and_36_out);
  and and_36 (and_36_out, nand_12_out, or_27_out);
  and and_37 (and_37_out, ~and_36_out, and_22_out);  // AND_Gate
  nand nand_12 (nand_12_out, A32, B32);
  or or_27 (or_27_out, A32, B32);
  or or_28 (_32, and_23_out, and_30_out, and_39_out);
  and and_38 (and_38_out, and_40_out, Shift_Right);
  and and_39 (and_39_out, Shift_Left, and_51_out);
  and and_40 (and_40_out, or_22_out, nand_9_out);
  or or_29 (or_29_out, Invert_Output, and_41_out);
  and and_41 (and_41_out, ~and_42_out, or_30_out);  // AND_Gate
  or or_30 (or_30_out, and_52_out, Half_Carry);
  and and_42 (and_42_out, and_52_out, Half_Carry);
  and and_43 (and_43_out, ~and_33_out, or_31_out);  // AND_Gate
  or or_31 (or_31_out, and_34_out, and_45_out);
  and and_44 (and_44_out, not_6_out, or_35_out);
  and and_45 (and_45_out, nand_11_out, or_32_out);
  or or_32 (or_32_out, B32, Invert_B);
  nand nand_13 (nand_13_out, Invert_A, A16);
  and and_46 (and_46_out, A16, and_37_out, and_47_out);
  and and_47 (and_47_out, nand_16_out, or_40_out);
  and and_48 (and_48_out, ~and_47_out, and_37_out);  // AND_Gate
  or or_33 (_16, and_38_out, and_49_out, and_56_out);
  and and_49 (and_49_out, not_4_out, not_3_out, and_51_out);
  and and_50 (and_50_out, and_51_out, Shift_Right);
  or or_34 (or_34_out, and_51_out, or_47_out);
  and and_51 (and_51_out, or_29_out, nand_14_out);
  nand nand_14 (nand_14_out, Invert_Output, and_41_out);
  and and_52 (and_52_out, ~and_53_out, or_36_out);  // AND_Gate
  or or_35 (or_35_out, and_42_out, and_53_out);
  and and_53 (and_53_out, and_54_out, not_5_out, and_55_out);
  or or_36 (or_36_out, and_54_out, and_55_out);
  and and_54 (and_54_out, nand_13_out, or_38_out);
  and and_55 (and_55_out, nand_15_out, or_37_out);
  or or_37 (or_37_out, B16, Invert_B);
  or or_38 (or_38_out, A16, Invert_A);
  nand nand_15 (nand_15_out, Invert_B, B16);
  or or_39 (or_39_out, or_26_out, and_46_out);
  nand nand_16 (nand_16_out, A16, B16);
  or or_40 (or_40_out, A16, B16);
  and and_56 (and_56_out, Shift_Left, and_68_out);
  and and_57 (and_57_out, not_4_out, not_3_out, and_68_out);
  or or_41 (or_41_out, Invert_Output, and_58_out);
  nand nand_17 (nand_17_out, Invert_Output, and_58_out);
  and and_58 (and_58_out, ~and_59_out, or_42_out);  // AND_Gate
  or or_42 (or_42_out, and_70_out, and_77_out);
  and and_59 (and_59_out, and_70_out, and_77_out);
  and and_60 (Half_Carry, not_6_out, or_43_out);
  or or_43 (or_43_out, and_59_out, and_61_out);
  and and_61 (and_61_out, and_62_out, not_5_out, and_71_out);
  and and_62 (and_62_out, nand_18_out, or_44_out);
  or or_44 (or_44_out, A8, Invert_A);
  nand nand_18 (nand_18_out, Invert_A, A8);
  and and_63 (and_63_out, A8, and_48_out, and_64_out);
  and and_64 (and_64_out, nand_20_out, or_45_out);
  and and_65 (and_65_out, ~and_64_out, and_48_out);  // AND_Gate
  or or_45 (or_45_out, A8, B8);
  or or_46 (_8, and_50_out, and_57_out, and_66_out);
  and and_66 (and_66_out, Shift_Left, and_73_out);
  and and_67 (and_67_out, and_68_out, Shift_Right);
  or or_47 (or_47_out, and_68_out, or_51_out);
  and and_68 (and_68_out, or_41_out, nand_17_out);
  and and_69 (and_69_out, ~and_74_out, or_53_out);  // AND_Gate
  and and_70 (and_70_out, ~and_61_out, or_48_out);  // AND_Gate
  or or_48 (or_48_out, and_62_out, and_71_out);
  and and_71 (and_71_out, nand_19_out, or_49_out);
  or or_49 (or_49_out, B8, Invert_B);
  nand nand_19 (nand_19_out, Invert_B, B8);
  or or_50 (or_50_out, or_39_out, and_63_out);
  nand nand_20 (nand_20_out, A8, B8);
  and and_72 (and_72_out, not_4_out, not_3_out, and_73_out);
  or or_51 (or_51_out, and_73_out, or_66_out);
  and and_73 (and_73_out, or_52_out, nand_21_out);
  or or_52 (or_52_out, Invert_Output, and_69_out);
  nand nand_21 (nand_21_out, Invert_Output, and_69_out);
  or or_53 (or_53_out, and_75_out, and_86_out);
  and and_74 (and_74_out, and_75_out, and_86_out);
  and and_75 (and_75_out, ~and_76_out, or_62_out);  // AND_Gate
  and and_76 (and_76_out, and_78_out, not_5_out, and_87_out);
  and and_77 (and_77_out, not_6_out, or_54_out);
  or or_54 (or_54_out, and_74_out, and_76_out);
  and and_78 (and_78_out, nand_23_out, or_55_out);
  or or_55 (or_55_out, A4, Invert_A);
  nand nand_22 (nand_22_out, Invert_B, B4);
  nand nand_23 (nand_23_out, Invert_A, A4);
  or or_56 (or_56_out, or_50_out, and_79_out);
  and and_79 (and_79_out, A4, and_65_out, and_80_out);
  and and_80 (and_80_out, nand_24_out, or_57_out);
  and and_81 (and_81_out, ~and_80_out, and_65_out);  // AND_Gate
  nand nand_24 (nand_24_out, A4, B4);
  or or_57 (or_57_out, A4, B4);
  or or_58 (_4, and_67_out, and_72_out, and_82_out);
  and and_82 (and_82_out, Shift_Left, and_94_out);
  and and_83 (and_83_out, and_73_out, Shift_Right);
  or or_59 (or_59_out, Invert_Output, and_84_out);
  and and_84 (and_84_out, ~and_85_out, or_60_out);  // AND_Gate
  or or_60 (or_60_out, and_95_out, and_102_out);
  and and_85 (and_85_out, and_95_out, and_102_out);
  or or_61 (or_61_out, and_85_out, and_96_out);
  or or_62 (or_62_out, and_78_out, and_87_out);
  and and_86 (and_86_out, not_6_out, or_61_out);
  and and_87 (and_87_out, nand_22_out, or_63_out);
  and and_88 (and_88_out, nand_25_out, or_68_out);
  or or_63 (or_63_out, B4, Invert_B);
  nand nand_25 (nand_25_out, Invert_A, A2);
  and and_89 (and_89_out, A2, and_81_out, and_90_out);
  and and_90 (and_90_out, nand_28_out, or_64_out);
  and and_91 (and_91_out, ~and_90_out, and_81_out);  // AND_Gate
  or or_64 (or_64_out, A2, B2);
  or or_65 (_2, and_83_out, and_92_out, and_99_out);
  and and_92 (and_92_out, not_4_out, not_3_out, and_94_out);
  and and_93 (and_93_out, and_94_out, Shift_Right);
  or or_66 (or_66_out, and_94_out, and_108_out);
  and and_94 (and_94_out, or_59_out, nand_26_out);
  nand nand_26 (nand_26_out, Invert_Output, and_84_out);
  and and_95 (and_95_out, ~and_96_out, or_67_out);  // AND_Gate
  or or_67 (or_67_out, and_88_out, and_97_out);
  and and_96 (and_96_out, and_88_out, not_5_out, and_97_out);
  and and_97 (and_97_out, nand_27_out, or_69_out);
  or or_68 (or_68_out, A2, Invert_A);
  or or_69 (or_69_out, B2, Invert_B);
  nand nand_27 (nand_27_out, Invert_B, B2);
  or or_70 (or_70_out, or_56_out, and_89_out);
  nand nand_28 (nand_28_out, A2, B2);
  and and_98 (and_98_out, not_4_out, not_3_out, and_108_out);
  and and_99 (and_99_out, Shift_Left, and_108_out);
  or or_71 (or_71_out, Invert_Output, and_100_out);
  nand nand_29 (nand_29_out, Invert_Output, and_100_out);
  and and_100 (and_100_out, ~and_101_out, or_72_out);  // AND_Gate
  or or_72 (or_72_out, and_109_out, Carry_In);
  and and_101 (and_101_out, and_109_out, Carry_In);
  and and_102 (and_102_out, not_6_out, or_73_out);
  and and_103 (and_103_out, and_104_out, not_5_out, and_110_out);
  or or_73 (or_73_out, and_101_out, and_103_out);
  and and_104 (and_104_out, nand_30_out, or_74_out);
  or or_74 (or_74_out, A1, Invert_A);
  nand nand_30 (nand_30_out, Invert_A, A1);
  or or_75 (A_B, or_70_out, and_105_out);
  and and_105 (and_105_out, A1, and_91_out, and_106_out);
  and and_106 (and_106_out, nand_31_out, or_76_out);
  and and_107 (A_B_2, ~and_106_out, and_91_out);  // AND_Gate
  nand nand_31 (nand_31_out, A1, B1);
  or or_76 (or_76_out, A1, B1);
  or or_77 (_1, and_93_out, and_98_out);
  not not_3 (not_3_out, Shift_Left);
  not not_4 (not_4_out, Shift_Right);
  and and_108 (and_108_out, or_71_out, nand_29_out);
  and and_109 (and_109_out, ~and_103_out, or_78_out);  // AND_Gate
  or or_78 (or_78_out, and_104_out, and_110_out);
  not not_5 (not_5_out, Inhibit_And);
  not not_6 (not_6_out, Inhibit_Carry);
  and and_110 (and_110_out, nand_32_out, or_79_out);
  or or_79 (or_79_out, B1, Invert_B);
  nand nand_32 (nand_32_out, Invert_B, B1);
  and and_111 (Sign, and_7_out, Carry_In, Invert_B);
endmodule
