// Logisim project shift-register.circ as structural Verilog: 1 circuit, main circuit main
module main (
  input  Carry,
  input  X7,
  input  X6,
  input  X5,
  input  X4,
  input  X3,
  input  X2,
  input  X1,
  input  X0,
  input  R,
  input  L,
  input  C,
  output Carry_prime,
  output X7_prime,
  output X6_prime,
  output X5_prime,
  output X4_prime,
  output X3_prime,
  output X2_prime,
  output X1_prime,
  output X0_prime
);

  wire and_1_out, and_2_out, and_3_out, and_4_out, and_5_out, and_6_out, and_7_out, and_8_out, and_9_out,
       and_10_out, and_11_out, and_12_out, and_13_out, and_14_out, and_15_out, and_16_out, and_17_out,
       and_18_out, and_19_out, and_20_out, and_21_out, and_22_out, and_23_out, and_24_out, and_25_out,
       and_26_out, and_27_out, not_1_out, not_2_out;

  not not_1 (not_1_out, R);
  not not_2 (not_2_out, L);
  and and_1 (and_1_out, L, X7);
  and and_2 (and_2_out, not_2_out, Carry, not_1_out);
  or or_1 (Carry_prime, and_27_out, and_2_out, and_1_out);
  and and_3 (and_3_out, C, Carry_prime, R);
  and and_4 (and_4_out, X7, R);
  and and_5 (and_5_out, not_2_out, X7, not_1_out);
  or or_2 (X7_prime, and_3_out, and_5_out, and_6_out);
  and and_6 (and_6_out, L, X6);
  and and_7 (and_7_out, not_2_out, X6, not_1_out);
  or or_3 (X6_prime, and_4_out, and_7_out, and_8_out);
  and and_8 (and_8_out, L, X5);
  and and_9 (and_9_out, X6, R);
  and and_10 (and_10_out, not_2_out, X5, not_1_out);
  and and_11 (and_11_out, X5, R);
  or or_4 (X5_prime, and_9_out, and_10_out, and_12_out);
  and and_12 (and_12_out, L, X4);
  and and_13 (and_13_out, X4, R);
  and and_14 (and_14_out, not_2_out, X4, not_1_out);
  or or_5 (X4_prime, and_11_out, and_14_out, and_15_out);
  and and_15 (and_15_out, L, X3);
  and and_16 (and_16_out, not_2_out, X3, not_1_out);
  or or_6 (X3_prime, and_13_out, and_16_out, and_18_out);
  and and_17 (and_17_out, X3, R);
  and and_18 (and_18_out, L, X2);
  and and_19 (and_19_out, not_2_out, X2, not_1_out);
  and and_20 (and_20_out, X2, R);
  or or_7 (X2_prime, and_17_out, and_19_out, and_22_out);
  and and_21 (and_21_out, not_2_out, X1, not_1_out);
  and and_22 (and_22_out, L, X1);
  or or_8 (X1_prime, and_20_out, and_21_out, and_24_out);
  and and_23 (and_23_out, X1, R);
  and and_24 (and_24_out, L, X0);
  and and_25 (and_25_out, not_2_out, X0, not_1_out);
  and and_26 (and_26_out, C, Carry_prime, L);
  or or_9 (X0_prime, and_23_out, and_25_out, and_26_out);
  and and_27 (and_27_out, X0, R);
endmodule
