// Logisim project test.circ as structural Verilog: 1 circuit, main circuit main
module main (
  output F2,
  output F1,
  output F0,
  output Cin,
  output M,
  output B7,
  output out_7,
  output out_8,
  output out_9,
  output out_10,
  output out_11,
  output out_12,
  output B0,
  output A7,
  output out_15,
  output out_16,
  output out_17,
  output out_18,
  output out_19,
  output out_20,
  output A0,
  output Zero,
  output A_B,
  output Carry,
  output Ovfl,
  output Sign,
  output S7,
  output out_28,
  output out_29,
  output out_30,
  output out_31,
  output out_32,
  output out_33,
  output S0
);

  wire clock_1_out, R_out;

  Clock clock_1 (.out(clock_1_out));
  Button R (.out(R_out));
  Counter #(.width(21), .max('h1fffff)) counter_1 (
    .load(1'b0), .count(1'b1),
    .Q({F2, F1, F0, Cin, M, B7, out_7, out_8, out_9, out_10, out_11, out_12, B0, A7, out_15, out_16, out_17, out_18, out_19, out_20, A0}),
    .clk(clock_1_out), .clr(R_out));  // open: D, carry
  // ALU alu_1: pin names not known; wires that end beside it: F2, F1, F0, Cin, M, B7, out_7, out_8, out_9, out_10, out_11, out_12, B0, A7, out_15, out_16, out_17, out_18, out_19, out_20, A0, Zero, A_B, Carry, Ovfl, Sign, S7, out_28, out_29, out_30, out_31, out_32, out_33, S0
endmodule
